# Fritzing sketch MusicalKeyboard (saved by Fritzing 0.6.3b)
breadboards: 1

parts:
  Arduino1 = Arduino
  S1 = Pushbutton [package="[THT]"]
  S2 = Pushbutton [package="[THT]"]
  S3 = Pushbutton [package="[THT]"]
  S4 = Pushbutton [package="[THT]"]
  S5 = Pushbutton [package="[THT]"]
  S6 = Pushbutton [package="[THT]"]
  J1 = Piezo Speaker
  R3 = Resistor [tolerance=±5% resistance=220 package=THT]
  R4 = Resistor [tolerance=±5% resistance=220 package=THT]
  R5 = Resistor [tolerance=±5% resistance=220 package=THT]
  R7 = Resistor [tolerance=±5% resistance=220 package=THT]
  R8 = Resistor [tolerance=±5% resistance=220 package=THT]
  R9 = Resistor [tolerance=±5% resistance=220 package=THT]

nets (from the breadboard view):
  N1: Arduino1.GND, J1.pin1, R3.Pin_0, R4.Pin_0, R5.Pin_0, R7.Pin_0, R8.Pin_0, R9.Pin_0
  N2: Arduino1.D9, J1.pin2
  N3: Arduino1.D8, S1.Pin_3, S1.Pin_4, R7.Pin_1
  N4: Arduino1.D7, S2.Pin_3, S2.Pin_4, R3.Pin_1
  N5: Arduino1.D6, S3.Pin_3, S3.Pin_4, R4.Pin_1
  N6: Arduino1.D5, S4.Pin_3, S4.Pin_4, R5.Pin_1
  N7: Arduino1.D4, S5.Pin_3, S5.Pin_4, R8.Pin_1
  N8: Arduino1.D3, S6.Pin_3, S6.Pin_4, R9.Pin_1
  N9: Arduino1.+5V, S1.Pin_1, S1.Pin_2, S2.Pin_1, S2.Pin_2, S3.Pin_1, S3.Pin_2, S4.Pin_1, S4.Pin_2, S5.Pin_1, S5.Pin_2, S6.Pin_1, S6.Pin_2
