# Fritzing sketch RgbLedPot (saved by Fritzing 0.6.3b)
breadboards: 1

parts:
  Arduino1 = Arduino
  R1 = Resistor [tolerance=±5% resistance=220 package=THT]
  R2 = Resistor [tolerance=±5% resistance=220 package=THT]
  R3 = Resistor [tolerance=±5% resistance=220 package=THT]
  LED1 = LED - 5mm [color="Red (633nm)" package="5 mm [THT]"]  # not connected
  LED2 = LED - 5mm [color="Green (555nm)" package="5 mm [THT]"]
  R4 = Rotary Potentiometer (Large) [maximum_resistance=100kΩ package=THT]
  LED3 = LED - 5mm [color="Blue (430nm)" package="5 mm [THT]"]

nets:
  N1: Arduino1.GND, R1.Pin_0, R2.Pin_0, R3.Pin_0, R4.leg2
  N2: Arduino1.D10, LED2.anode
  N3: Arduino1.D9, LED3.anode
  N4: Arduino1.+5V, R4.leg1
  N5: Arduino1.A0, R4.wiper
  N6: R2.Pin_1, LED2.cathode
  N7: R3.Pin_1, LED3.cathode
